# Fritzing sketch esp8266_sp01_postload (saved by Fritzing 0.9.2b)
breadboards: 1

parts:
  Parte1 = Arduino Uno (Rev3)
  U1 = ESP8266 WiFi Module [part_number=ESP8266]
  Parte2 = SRF05 Ultrasonic Rangefinder

nets:
  GND: Parte1.GND, Parte1.RESET, Parte2.GND
  N1: Parte1.D0/RX, U1.RXD
  N2: Parte1.D1/TX, U1.TXD
  3V3: Parte1.3V3, U1.VCC, U1.CH_PD
  5V: Parte1.5V, Parte2.VCC
  N3: U1.GPIO_0, Parte2.Echo
  N4: U1.GPIO_2, Parte2.Trig

custom parts:
  ESP8266 WiFi Module: Generic WiFi Module based on the ESP8266 with onboard PCB antenna and UART communications
